# Fritzing sketch Automatic Nightlight (saved by Fritzing 0.9.3b)
breadboards: 1

parts:
  Part1 = Arduino Uno (Rev3)
  R1 = Resistor [tolerance=±5% resistance=220 package="2010 [SMD]"]
  R2 = Resistor [tolerance=±5% resistance=220 package="2010 [SMD]"]
  R3 = Resistor [tolerance=±5% resistance=220 package="2010 [SMD]"]
  LED2 = RGB LED - (4 legs) [package="5 mm [THT]"]
  R4 = Resistor [tolerance=±5% resistance=220 package="1206 [SMD]"]
  R5 = PHOTOCELL [package=photocell]

nets:
  N1: Part1.A0, R4.Pin_0, R5.P$2
  N2: Part1.D9_PWM, R2.Pin_1
  N3: Part1.GND, LED2.common_anode, R4.Pin_1
  N4: Part1.D0/RX, R3.Pin_1
  N5: Part1.D1/TX, R1.Pin_1
  N6: Part1.5V, R5.P$1
  N7: R1.Pin_0, LED2.red_cathode
  N8: R2.Pin_0, LED2.blue_cathode
  N9: R3.Pin_0, LED2.green_cathode
